// Logisim project decoder dado.circ as structural Verilog: 2 circuits, main circuit main
module main (
  input  [2:0] A,
  output L1,
  output L2,
  output L3,
  output L4,
  output L5,
  output L6,
  output L7
);

  or or_1 (L1, A[2], A[1]);
  and and_1 (L2, A[2], A[1]);

  assign L3 = A[2];
  assign L4 = A[0];
  assign L5 = A[2];
  assign L6 = L2;
  assign L7 = L1;
endmodule

module decoder_dado (
);

  wire clock_1_out, main_1_l1, main_1_l2, main_1_l3, main_1_l4, main_1_l5, main_1_l6, main_1_l7;
  wire [2:0] random_1_out;

  Clock #(.highDuration(3), .lowDuration(3)) clock_1 (.out(clock_1_out));
  Random #(.width(3)) random_1 (.out(random_1_out));  // open: clk, next, clr
  LED led_1 (.in(main_1_l1));
  main main_1 (
    .A(random_1_out), .L1(main_1_l1), .L2(main_1_l2), .L3(main_1_l3), .L4(main_1_l4), .L5(main_1_l5),
    .L6(main_1_l6), .L7(main_1_l7));
  LED led_2 (.in(main_1_l2));
  LED led_3 (.in(main_1_l3));
  LED led_4 (.in(main_1_l5));
  LED led_5 (.in(main_1_l4));
  LED led_6 (.in(main_1_l7));
  LED led_7 (.in(main_1_l6));
endmodule
